// Digital circuit dice.dig as structural Verilog
module dice (
  input  clk
);

  wire and_1_out;
  wire [7:0] _0_35_out;

  and and_1 (and_1_out, _0_35_out[2], _0_35_out[5]);
  Counter #(.Bits(8)) _0_35 (.en(1'b1), .C(clk), .clr(and_1_out), .out(_0_35_out));  // open: ovf
  ROM #(.AddrBits(8), .Bits(8)) rom_1 (.A(_0_35_out), .sel(1'b1));  // open: D
  LED led_1 (.in(_0_35_out[0]));
  LED led_2 (.in(_0_35_out[1]));
  LED led_3 (.in(_0_35_out[2]));
  LED led_4 (.in(_0_35_out[3]));
  LED led_5 (.in(_0_35_out[4]));
  LED led_6 (.in(_0_35_out[5]));

  // Notes on the sheet:
  //   clk: Hz: 5
endmodule
