// Digital circuit dice2.dig as structural Verilog
module dice2 (
  input  clk
);

  wire _0_35_ovf, and_1_out, and_2_out, button_1_out;
  wire [3:0] rom_1_d;
  wire [6:0] switch_1_b;
  wire [15:4] rom_1_d_2;

  Button button_1 (.out(button_1_out));
  and and_1 (and_1_out, clk, button_1_out);
  Counter #(.Bits(6)) _0_35 (.en(1'b1), .C(and_1_out), .clr(and_2_out), .out(switch_1_b[5:0]), .ovf(_0_35_ovf));
  Switch switch_1 (.A(1'b1), .B(switch_1_b[6]));
  LED led_1 (.in(_0_35_ovf));
  and and_2 (and_2_out, switch_1_b[2], switch_1_b[5]);
  LED led_2 (.in(rom_1_d_2[14]));
  LED led_3 (.in(rom_1_d_2[15]));
  LED led_4 (.in(rom_1_d_2[13]));
  ROM #(.AddrBits(7), .Bits(16)) rom_1 (.A(switch_1_b), .sel(1'b1), .D({rom_1_d_2, rom_1_d}));
  Seven_Seg seven_seg_1 (
    .a(1'b0), .b(rom_1_d_2[7]), .c(rom_1_d_2[7]), .d(1'b0), .e(1'b0), .f(1'b0), .g(1'b0), .dp(1'b0));
  LED led_5 (.in(rom_1_d_2[13]));
  LED led_6 (.in(rom_1_d_2[12]));
  LED led_7 (.in(rom_1_d_2[15]));
  LED led_8 (.in(rom_1_d_2[14]));
  Seven_Seg seven_seg_2 (
    .a(rom_1_d[3]), .b(rom_1_d[2]), .c(rom_1_d[1]), .d(rom_1_d[0]), .e(rom_1_d_2[4]), .f(rom_1_d_2[5]),
    .g(rom_1_d_2[6]), .dp(1'b0));
  LED led_9 (.in(rom_1_d_2[10]));
  LED led_10 (.in(rom_1_d_2[11]));
  LED led_11 (.in(rom_1_d_2[9]));
  LED led_12 (.in(rom_1_d_2[9]));
  LED led_13 (.in(rom_1_d_2[8]));
  LED led_14 (.in(rom_1_d_2[11]));
  LED led_15 (.in(rom_1_d_2[10]));

  // Notes on the sheet:
  //   clk: Hz: 50000
  //   contents of rom_1 (hex, n*v repeats v):
  //   106,25d,34f,666,76b,e7b,106,25d,34f,666,76b,e7b,106,25d,34f,666,76b,e7b,106,25d,34f,
  //   666,76b,e7b,106,25d,34f,666,76b,e7b,106,25d,34f,666,76b,e7b,0,0,0,0,0,0,0,0,0,0,0,
  //   0,0,0,0,0,0,0,0,0,0,0,0,0,0,0,0,0,115d,124f,1366,166b,177b,1e0e,214f,2266,236b,267b,
  //   270e,2e7f,3166,326b,337b,360e,377f,3e6f,616b,627b,630e,667f,676f,6ebf,717b,720e,737f,
  //   766f,77bf,7e86,e10e,e27f,e36f,e6bf,e786,eedd,ffff,ffff,ffff,ffff,ffff,ffff,ffff,ffff,
  //   ffff,ffff,ffff,ffff,ffff,ffff,ffff,ffff,ffff,ffff,ffff,ffff,ffff,ffff,ffff,ffff,ffff,
  //   ffff,ffff,ffff
endmodule
